// Logisim project GshareGiven.circ as structural Verilog: 7 circuits, main circuit main
module main (
);

  wire Clock, Correct, CorrectPred, Done, gsharepredictor_1_takebranch, inputgen_1_branchtaken,
       inputgen_1_isbranch, IsPredBranchCorrect, IsPredCorrect, not_1_out;
  wire [31:0] CorrectPredBranch, gsharepredictor_1_predbranchdest, inputgen_1_branchdestaddress,
       inputgen_1_predpc, inputgen_1_updatepc;

  InputGen inputgen_1 (
    .Clock(Clock), .PredPC(inputgen_1_predpc), .UpdatePC(inputgen_1_updatepc),
    .IsBranch(inputgen_1_isbranch), .BranchTaken(inputgen_1_branchtaken),
    .BranchDestAddress(inputgen_1_branchdestaddress));
  GsharePredictor gsharepredictor_1 (
    .PredPC(inputgen_1_predpc), .UpdatePC(inputgen_1_updatepc), .IsBranch(inputgen_1_isbranch),
    .BranchTaken(inputgen_1_branchtaken), .BranchDestAddr(inputgen_1_branchdestaddress), .Clock(Clock),
    .TakeBranch(gsharepredictor_1_takebranch), .PredBranchDest(gsharepredictor_1_predbranchdest));
  Clock clock_1 (.out(Clock));
  Test test_1 (
    .TakeBranch(gsharepredictor_1_takebranch), .PredBranchAddress(gsharepredictor_1_predbranchdest),
    .Clock(Clock), .IsPredCorrect(IsPredCorrect), .CorrectPred(CorrectPred),
    .IsPredBranchCorrect(IsPredBranchCorrect), .CorrectPredBranch(CorrectPredBranch), .Correct(Correct),
    .Done(Done));
  not not_1 (not_1_out, Done);
  Shift_Register #(.length(28)) shift_register_1 (
    .shift(not_1_out), .in(Correct), .clk(Clock));  // open: out, load, clr, d0, q0, d1, q1, d2, q2, d3, q3, d4, q4, d5, q5, d6, q6, d7, q7, d8, q8, d9, q9, d10, q10, d11, q11, d12, q12, d13, q13, d14, q14, d15, q15, d16, q16, d17, q17, d18, q18, d19, q19, d20, q20, d21, q21, d22, q22, d23, q23, d24, q24, d25, q25, d26, q26, d27, q27
  // Probe on IsPredCorrect
  // Probe on CorrectPred
  // Probe on IsPredBranchCorrect
  // Probe on CorrectPredBranch
  // Probe on Correct
  // Probe on Done
endmodule

module GsharePredictor (
  input  [31:0] PredPC,
  input  [31:0] UpdatePC,
  input  IsBranch,
  input  BranchTaken,
  input  [31:0] BranchDestAddr,
  input  Clock,
  output TakeBranch,
  output [31:0] PredBranchDest
);

  wire and_1_out, comparator_1_eq, comparator_1_gt, CounterData, not_1_out, not_2_out, not_3_out, not_4_out,
       TagData;
  wire [1:0] BrHistData, counters_1_countdata, Index;
  wire [31:0] tagregisters_1_countdata;

  assign Index = PredPC[1:0] ^ BrHistData;  // XOR_Gate xor_1, 2 bits wide
  Counters counters_1 (
    .in_4(Index), .in_5(not_1_out), .CountData(counters_1_countdata));  // open: in_2, in_3, in_6, in_1
  not not_1 (not_1_out, Clock);
  TagRegisters tagregisters_1 (
    .in_2(Index), .in_4(not_2_out), .CountData(tagregisters_1_countdata));  // open: in_1, in_3, in_5
  not not_2 (not_2_out, Clock);
  BranchDestRegs branchdestregs_1 (
    .in_2(Index), .in_4(not_3_out), .CountData(PredBranchDest));  // open: in_1, in_3, in_5
  not not_3 (not_3_out, Clock);
  Comparator #(.width(2), .mode("unsigned")) comparator_1 (
    .a(counters_1_countdata), .b(2'b10), .gt(comparator_1_gt), .eq(comparator_1_eq));  // open: lt
  or or_1 (CounterData, comparator_1_gt, comparator_1_eq);
  Comparator #(.width(32), .mode("unsigned")) comparator_2 (
    .a(tagregisters_1_countdata), .b(PredPC), .eq(TagData));  // open: gt, lt
  not not_4 (not_4_out, Clock);
  Register #(.width(2)) Branch_History_Register (
    .D({BrHistData[0], BranchTaken}), .Q(BrHistData), .clk(and_1_out));  // open: en, clr
  and and_1 (and_1_out, not_4_out, IsBranch);
  and and_2 (TakeBranch, CounterData, TagData, IsBranch);

  // Other names for the same wires on the sheet: BranchDestData[31:0] = PredBranchDest
endmodule

module InputGen (
  input  Clock,
  output [31:0] PredPC,
  output [31:0] UpdatePC,
  output IsBranch,
  output BranchTaken,
  output [31:0] BranchDestAddress
);

  wire [7:0] counter_1_q;

  Counter #(.max('h1b), .ongoal("stay")) counter_1 (
    .count(1'b1), .Q(counter_1_q), .clk(Clock));  // open: load, D, carry, clr
  ROM #(.dataWidth(32)) rom_1 (.addr(counter_1_q), .data(PredPC));  // open: sel
  ROM #(.dataWidth(1)) rom_2 (.addr(counter_1_q), .data(IsBranch));  // open: sel
  ROM #(.dataWidth(1)) rom_3 (.addr(counter_1_q), .data(BranchTaken));  // open: sel
  ROM #(.dataWidth(32)) rom_4 (.addr(counter_1_q), .data(BranchDestAddress));  // open: sel

  assign UpdatePC = PredPC;

  // Notes on the sheet:
  //   Counter max count is 27 because there are only 28 instructions
  //   contents of rom_1 (hex, n*v repeats v):
  //   5*0 1 1 1 5 2 2 2 3 3 3 0 0 4
  //   contents of rom_2 (hex, n*v repeats v):
  //   8*1 0 8*1 0 10*1
  //   contents of rom_3 (hex, n*v repeats v):
  //   8*1 0 6*1 4*0 1 0 1 0 1 0 1 0 1
  //   contents of rom_4 (hex, n*v repeats v):
  //   5*60 5f 5f 5f 0 5 5 5 8 8 8 60 60 0 10*60
endmodule

module Test (
  input  TakeBranch,
  input  [31:0] PredBranchAddress,
  input  Clock,
  output IsPredCorrect,
  output CorrectPred,
  output IsPredBranchCorrect,
  output [31:0] CorrectPredBranch,
  output Correct,
  output Done
);

  wire comparator_1_eq, comparator_2_eq, DontCare, not_1_out;
  wire [7:0] Count;

  Counter #(.max('h1c), .ongoal("stay")) counter_1 (.count(1'b1), .Q(Count), .clk(Clock));  // open: load, D, carry, clr
  ROM #(.dataWidth(1)) rom_1 (.addr(Count), .data(CorrectPred));  // open: sel
  ROM #(.dataWidth(32)) rom_2 (.addr(Count), .data(CorrectPredBranch));  // open: sel
  ROM #(.dataWidth(1)) rom_3 (.addr(Count), .data(DontCare));  // open: sel
  not not_1 (not_1_out, CorrectPred);
  Comparator #(.width(1), .mode("unsigned")) comparator_1 (
    .a(TakeBranch), .b(CorrectPred), .eq(comparator_1_eq));  // open: gt, lt
  or or_1 (IsPredCorrect, comparator_1_eq, DontCare);
  Comparator #(.width(32), .mode("unsigned")) comparator_2 (
    .a(PredBranchAddress), .b(CorrectPredBranch), .eq(comparator_2_eq));  // open: gt, lt
  Comparator #(.mode("unsigned")) comparator_3 (.a(Count), .b(8'h1c), .eq(Done));  // open: gt, lt
  // Probe on Count
  or or_2 (IsPredBranchCorrect, comparator_2_eq, not_1_out, DontCare);
  and and_1 (Correct, IsPredCorrect, IsPredBranchCorrect);

  // Notes on the sheet:
  //   Correct Take Branch
  //   Correct Prediction Branch Address
  //   Don't Care
  //   contents of rom_1 (hex, n*v repeats v):
  //   4*0 1 0 0 1 0 0 0 1 0 0 1 1 9*0 1 0 1
  //   contents of rom_2 (hex, n*v repeats v):
  //   0 0 0 60 60 0 5f 5f 5f 60 5 5 60 8 8 60 5f 8 8 60 5 7*60
  //   contents of rom_3 (hex, n*v repeats v):
  //   8*0 1 8*0 1
endmodule

module Counters (
  input  [1:0] in_1,
  input  in_2,
  input  [1:0] in_3,
  input  [1:0] in_4,
  input  in_5,
  input  in_6,
  output [1:0] CountData
);

  wire Count0, Count1, Count2, Count3;
  wire [1:0] CntData0, CntData1, CntData2, CntData3;

  Demultiplexer #(.select(2), .enable("false")) demultiplexer_1 (
    .out0(Count0), .out1(Count1), .out2(Count2), .out3(Count3), .in(in_6), .sel(in_3));
  Counter #(.width(2), .max('h3), .ongoal("stay")) counter_1 (
    .load(in_2), .D(in_1), .count(Count0), .Q(CntData0), .clk(in_5));  // open: carry, clr
  Counter #(.width(2), .max('h3), .ongoal("stay")) counter_2 (
    .load(in_2), .count(Count1), .Q(CntData1), .clk(in_5));  // open: D, carry, clr
  Counter #(.width(2), .max('h3), .ongoal("stay")) counter_3 (
    .load(in_2), .count(Count2), .Q(CntData2), .clk(in_5));  // open: D, carry, clr
  Counter #(.width(2), .max('h3), .ongoal("stay")) counter_4 (
    .load(in_2), .count(Count3), .Q(CntData3), .clk(in_5));  // open: D, carry, clr
  Multiplexer #(.select(2), .width(2), .enable("false")) multiplexer_1 (
    .in0(CntData0), .in1(CntData1), .in2(CntData2), .in3(CntData3), .out(CountData), .sel(in_4));

  // Other names for the same wires on the sheet: clock = in_5; Increment_Decrement = in_2; ReadAddress[1:0] = in_4;
  //   WrCnt = in_6; WriteAddress[1:0] = in_3
endmodule

module TagRegisters (
  input  [1:0] in_1,
  input  [1:0] in_2,
  input  [31:0] in_3,
  input  in_4,
  input  in_5,
  output [31:0] CountData
);

  wire WrTag0, WrTag1, WrTag2, WrTag3;
  wire [31:0] TagData0, TagData1, TagData3, TagtData2;

  Demultiplexer #(.select(2), .enable("false")) demultiplexer_1 (
    .out0(WrTag0), .out1(WrTag1), .out2(WrTag2), .out3(WrTag3), .in(in_5), .sel(in_1));
  Register #(.width(32)) register_1 (.D(in_3), .en(WrTag0), .Q(TagData0), .clk(in_4));  // open: clr
  Register #(.width(32)) register_2 (.D(in_3), .en(WrTag1), .Q(TagData1), .clk(in_4));  // open: clr
  Register #(.width(32)) register_3 (.D(in_3), .en(WrTag2), .Q(TagtData2), .clk(in_4));  // open: clr
  Register #(.width(32)) register_4 (.D(in_3), .en(WrTag3), .Q(TagData3), .clk(in_4));  // open: clr
  Multiplexer #(.select(2), .width(32), .enable("false")) multiplexer_1 (
    .in0(TagData0), .in1(TagData1), .in2(TagtData2), .in3(TagData3), .out(CountData), .sel(in_2));

  // Other names for the same wires on the sheet: clock = in_4; ReadAddress[1:0] = in_2; WriteAddress[1:0] = in_1;
  //   WriteData[31:0] = in_3; WrTag = in_5
endmodule

module BranchDestRegs (
  input  [1:0] in_1,
  input  [1:0] in_2,
  input  [31:0] in_3,
  input  in_4,
  input  in_5,
  output [31:0] CountData
);

  wire WrTag0, WrTag1, WrTag2, WrTag3;
  wire [31:0] TagData0, TagData1, TagData3, TagtData2;

  Demultiplexer #(.select(2), .enable("false")) demultiplexer_1 (
    .out0(WrTag0), .out1(WrTag1), .out2(WrTag2), .out3(WrTag3), .in(in_5), .sel(in_1));
  Register #(.width(32)) register_1 (.D(in_3), .en(WrTag0), .Q(TagData0), .clk(in_4));  // open: clr
  Register #(.width(32)) register_2 (.D(in_3), .en(WrTag1), .Q(TagData1), .clk(in_4));  // open: clr
  Register #(.width(32)) register_3 (.D(in_3), .en(WrTag2), .Q(TagtData2), .clk(in_4));  // open: clr
  Register #(.width(32)) register_4 (.D(in_3), .en(WrTag3), .Q(TagData3), .clk(in_4));  // open: clr
  Multiplexer #(.select(2), .width(32), .enable("false")) multiplexer_1 (
    .in0(TagData0), .in1(TagData1), .in2(TagtData2), .in3(TagData3), .out(CountData), .sel(in_2));

  // Other names for the same wires on the sheet: clock = in_4; ReadAddress[1:0] = in_2; WriteAddress[1:0] = in_1;
  //   WriteData[31:0] = in_3; WrTag = in_5
endmodule
